// Logisim project Pong.circ as structural Verilog: 18 circuits, main circuit GPRenv
module REG_Compatible2 (
  input  [1:0] in_1,
  input  in_2,
  input  in_3,
  output [1:0] out_4
);

  Register #(.width(2)) register_1 (.D(in_1), .en(in_2), .clk(in_3), .Q(out_4), .clr(1'b0));
endmodule

module REG_Compatible8 (
  input  [7:0] in_1,
  input  in_2,
  input  in_3,
  output [7:0] out_4
);

  Register register_1 (.D(in_1), .en(in_2), .clk(in_3), .Q(out_4), .clr(1'b0));
endmodule

module REG_Compatible (
  input  [31:0] Data_In,
  input  WE,
  input  clk,
  output [31:0] Data_Out
);

  Register #(.width(32)) register_1 (.D(Data_In), .en(WE), .clk(clk), .Q(Data_Out), .clr(1'b0));
endmodule

module ReadWriteRegister32 (
  input  [31:0] WriteData,
  input  Str,
  input  [4:0] WriteAddr,
  input  [4:0] ReadAddr,
  input  Clk,
  output [31:0] WriteDataOut,
  output [31:0] ReadData,
  output StrOut,
  output [4:0] WriteAddrOut,
  output ClkOut
);

  wire RI0, RI1, RI2, RI3, RI4, RI5, RI6, RI7, RI8, RI9, RI10, RI11, RI12, RI13, RI14, RI15, RI16, RI17,
       RI18, RI19, RI20, RI21, RI22, RI23, RI24, RI25, RI26, RI27, RI28, RI29, RI30, RI31;
  wire [31:0] RO0, RO1, RO2, RO3, RO4, RO5, RO6, RO7, RO8, RO9, RO10, RO11, RO12, RO13, RO14, RO15, RO16,
       RO17, RO18, RO19, RO20, RO21, RO22, RO23, RO24, RO25, RO26, RO27, RO28, RO29, RO30, RO31;

  Demultiplexer #(.select(5)) demultiplexer_1 (
    .out0(RI0), .out1(RI1), .out2(RI2), .out3(RI3), .out4(RI4), .out5(RI5), .out6(RI6), .out7(RI7),
    .out8(RI8), .out9(RI9), .out10(RI10), .out11(RI11), .out12(RI12), .out13(RI13), .out14(RI14),
    .out15(RI15), .out16(RI16), .out17(RI17), .out18(RI18), .out19(RI19), .out20(RI20), .out21(RI21),
    .out22(RI22), .out23(RI23), .out24(RI24), .out25(RI25), .out26(RI26), .out27(RI27), .out28(RI28),
    .out29(RI29), .out30(RI30), .out31(RI31), .in(Str), .sel(WriteAddr));  // open: en
  REG_Compatible reg_compatible_1 (.Data_Out(RO0), .WE(RI0), .clk(Clk), .Data_In(WriteData));
  REG_Compatible reg_compatible_2 (.Data_Out(RO1), .WE(RI1), .clk(Clk), .Data_In(WriteData));
  REG_Compatible reg_compatible_3 (.Data_Out(RO2), .WE(RI2), .clk(Clk), .Data_In(WriteData));
  REG_Compatible reg_compatible_4 (.Data_Out(RO3), .WE(RI3), .clk(Clk), .Data_In(WriteData));
  REG_Compatible reg_compatible_5 (.Data_Out(RO4), .WE(RI4), .clk(Clk), .Data_In(WriteData));
  REG_Compatible reg_compatible_6 (.Data_Out(RO5), .WE(RI5), .clk(Clk), .Data_In(WriteData));
  REG_Compatible reg_compatible_7 (.Data_Out(RO6), .WE(RI6), .clk(Clk), .Data_In(WriteData));
  REG_Compatible reg_compatible_8 (.Data_Out(RO7), .WE(RI7), .clk(Clk), .Data_In(WriteData));
  REG_Compatible reg_compatible_9 (.Data_Out(RO8), .WE(RI8), .clk(Clk), .Data_In(WriteData));
  REG_Compatible reg_compatible_10 (.Data_Out(RO9), .WE(RI9), .clk(Clk), .Data_In(WriteData));
  REG_Compatible reg_compatible_11 (.Data_Out(RO10), .WE(RI10), .clk(Clk), .Data_In(WriteData));
  REG_Compatible reg_compatible_12 (.Data_Out(RO11), .WE(RI11), .clk(Clk), .Data_In(WriteData));
  REG_Compatible reg_compatible_13 (.Data_Out(RO12), .WE(RI12), .clk(Clk), .Data_In(WriteData));
  REG_Compatible reg_compatible_14 (.Data_Out(RO13), .WE(RI13), .clk(Clk), .Data_In(WriteData));
  REG_Compatible reg_compatible_15 (.Data_Out(RO14), .WE(RI14), .clk(Clk), .Data_In(WriteData));
  REG_Compatible reg_compatible_16 (.Data_Out(RO15), .WE(RI15), .clk(Clk), .Data_In(WriteData));
  REG_Compatible reg_compatible_17 (.Data_Out(RO16), .WE(RI16), .clk(Clk), .Data_In(WriteData));
  REG_Compatible reg_compatible_18 (.Data_Out(RO17), .WE(RI17), .clk(Clk), .Data_In(WriteData));
  REG_Compatible reg_compatible_19 (.Data_Out(RO18), .WE(RI18), .clk(Clk), .Data_In(WriteData));
  REG_Compatible reg_compatible_20 (.Data_Out(RO19), .WE(RI19), .clk(Clk), .Data_In(WriteData));
  REG_Compatible reg_compatible_21 (.Data_Out(RO20), .WE(RI20), .clk(Clk), .Data_In(WriteData));
  REG_Compatible reg_compatible_22 (.Data_Out(RO21), .WE(RI21), .clk(Clk), .Data_In(WriteData));
  REG_Compatible reg_compatible_23 (.Data_Out(RO22), .WE(RI22), .clk(Clk), .Data_In(WriteData));
  REG_Compatible reg_compatible_24 (.Data_Out(RO23), .WE(RI23), .clk(Clk), .Data_In(WriteData));
  REG_Compatible reg_compatible_25 (.Data_Out(RO24), .WE(RI24), .clk(Clk), .Data_In(WriteData));
  REG_Compatible reg_compatible_26 (.Data_Out(RO25), .WE(RI25), .clk(Clk), .Data_In(WriteData));
  REG_Compatible reg_compatible_27 (.Data_Out(RO26), .WE(RI26), .clk(Clk), .Data_In(WriteData));
  REG_Compatible reg_compatible_28 (.Data_Out(RO27), .WE(RI27), .clk(Clk), .Data_In(WriteData));
  REG_Compatible reg_compatible_29 (.Data_Out(RO28), .WE(RI28), .clk(Clk), .Data_In(WriteData));
  REG_Compatible reg_compatible_30 (.Data_Out(RO29), .WE(RI29), .clk(Clk), .Data_In(WriteData));
  REG_Compatible reg_compatible_31 (.Data_Out(RO30), .WE(RI30), .clk(Clk), .Data_In(WriteData));
  REG_Compatible reg_compatible_32 (.Data_Out(RO31), .WE(RI31), .clk(Clk), .Data_In(WriteData));
  Multiplexer #(.select(5), .width(32), .enable("false")) multiplexer_1 (
    .in0(RO0), .in1(RO1), .in2(RO2), .in3(RO3), .in4(RO4), .in5(RO5), .in6(RO6), .in7(RO7), .in8(RO8),
    .in9(RO9), .in10(RO10), .in11(RO11), .in12(RO12), .in13(RO13), .in14(RO14), .in15(RO15), .in16(RO16),
    .in17(RO17), .in18(RO18), .in19(RO19), .in20(RO20), .in21(RO21), .in22(RO22), .in23(RO23), .in24(RO24),
    .in25(RO25), .in26(RO26), .in27(RO27), .in28(RO28), .in29(RO29), .in30(RO30), .in31(RO31),
    .out(ReadData), .sel(ReadAddr));

  assign ClkOut = Clk;
  assign StrOut = Str;
  assign WriteAddrOut = WriteAddr;
  assign WriteDataOut = WriteData;
endmodule

module GPRenv (
  input  CLK,
  input  [31:0] C,
  input  [4:0] Badr,
  input  [4:0] Aadr,
  input  [4:0] Cadr,
  input  GPR_WE,
  output ClkOut,
  output [31:0] Cout,
  output [31:0] B,
  output [31:0] A,
  output [4:0] CadrOut,
  output AEQ,
  output GPR_WE_out
);

  wire and_1_out, or_1_out, readwriteregister32_2_clkout, readwriteregister32_2_strout;
  wire [4:0] readwriteregister32_2_writeaddrout;
  wire [31:0] ram_1_data;

  or or_1 (or_1_out, Cadr[0], Cadr[4]);
  and and_1 (and_1_out, or_1_out, GPR_WE);
  RAM #(.addrWidth(5), .dataWidth(32)) ram_1 (
    .addr(readwriteregister32_2_writeaddrout), .we(readwriteregister32_2_strout), .oe(1'b0),
    .clk(readwriteregister32_2_clkout), .data(ram_1_data));
  ReadWriteRegister32 readwriteregister32_1 (
    .WriteAddr(Cadr), .ReadAddr(Badr), .Clk(CLK), .ReadData(B), .Str(and_1_out), .WriteData(C));  // open: WriteDataOut, StrOut, WriteAddrOut, ClkOut
  ReadWriteRegister32 readwriteregister32_2 (
    .WriteAddr(Cadr), .ReadAddr(Aadr), .Clk(CLK), .ReadData(A), .Str(and_1_out), .WriteData(C),
    .WriteDataOut(ram_1_data), .StrOut(readwriteregister32_2_strout),
    .WriteAddrOut(readwriteregister32_2_writeaddrout), .ClkOut(readwriteregister32_2_clkout));
  Comparator #(.width(32), .mode("unsigned")) comparator_1 (.a(A), .b(B), .eq(AEQ));  // open: gt, lt

  assign CadrOut = Cadr;
  assign ClkOut = CLK;
  assign Cout = C;
  assign GPR_WE_out = GPR_WE;
endmodule

module IRenv (
  input  [31:0] DI,
  output [31:0] Inst,
  output [5:0] \function ,
  output JAL,
  output [4:0] Cadr,
  output [4:0] Badr,
  output [4:0] Aadr,
  output [5:0] opcode,
  output [31:0] Imm
);

  wire and_1_out, and_2_out, comparator_1_eq, nor_1_out, not_1_out, not_2_out, not_3_out;
  wire [4:0] multiplexer_1_out;

  Comparator #(.width(6), .mode("unsigned")) comparator_1 (
    .a({6{1'b0}}), .b(DI[31:26]), .eq(comparator_1_eq));  // open: gt, lt
  not not_1 (not_1_out, comparator_1_eq);
  Multiplexer #(.width(5), .enable("false")) multiplexer_1 (
    .in0(DI[15:11]), .in1(DI[20:16]), .out(multiplexer_1_out), .sel(not_1_out));
  assign Imm = {{16{DI[15]}}, DI[15:0]};  // Bit_Extender bit_extender_1
  not not_2 (not_2_out, DI[31]);
  not not_3 (not_3_out, DI[28]);
  and and_1 (and_1_out, not_2_out, not_3_out, DI[27], DI[26]);
  or or_1 (JAL, and_1_out, and_2_out);
  Multiplexer #(.width(5), .enable("false")) multiplexer_2 (
    .in0(multiplexer_1_out), .in1({5{1'b1}}), .out(Cadr), .sel(JAL));
  nor nor_1 (nor_1_out, DI[31], DI[30], DI[29], DI[28], DI[27], DI[26]);
  and and_2 (and_2_out, DI[3], DI[0], nor_1_out);

  assign Aadr = DI[25:21];
  assign Badr = DI[20:16];
  assign \function  = DI[5:0];
  assign Inst = DI;
  assign opcode = DI[31:26];
endmodule

module MEMenv (
  input  [31:0] IN,
  input  [31:0] ADDRESS,
  input  [31:0] MDO,
  input  MW,
  input  MR,
  input  CLK,
  output [31:0] MDI,
  output [11:0] MA,
  output [31:0] OUT,
  output strO,
  output ldO,
  output clkO
);


  assign clkO = CLK;
  assign ldO = MR;
  assign MA = ADDRESS[13:2];
  assign MDI = IN;
  assign OUT = MDO;
  assign strO = MW;
endmodule

module MEMenv2 (
  input  [31:0] in_1,
  input  [31:0] IN,
  input  [31:0] ADDRESS,
  input  MW,
  input  MR,
  input  CLK,
  input  [1:0] Xcoord,
  input  [1:0] Ycoord,
  output [31:0] out_9,
  output [11:0] out_10,
  output out_11,
  output out_12,
  output out_13,
  output [31:0] OUT,
  output [31:0] out_15,
  output [4:0] out_16,
  output out_17,
  output out_18,
  output [3:0] HEXlow,
  output [3:0] HEXhigh
);

  wire and_4_out, comparator_1_eq, comparator_2_eq, comparator_3_eq, comparator_4_eq, comparator_5_eq,
       or_2_out;
  wire [1:0] and_5_out, and_6_out, bit_extender_1_out, bit_extender_2_out, reg_compatible2_1_out_4,
       reg_compatible2_2_out_4;
  wire [31:0] bit_extender_3_out, bit_extender_4_out, or_1_out;

  Comparator #(.width(18), .mode("unsigned")) comparator_1 (
    .a(ADDRESS[31:14]), .b(18'h4004), .eq(comparator_1_eq));  // open: gt, lt
  Comparator #(.width(27), .mode("unsigned")) comparator_2 (
    .a(ADDRESS[31:5]), .b(27'h80), .eq(comparator_2_eq));  // open: gt, lt
  Comparator #(.width(32), .mode("unsigned")) comparator_3 (
    .a(ADDRESS), .b(32'h10012000), .eq(comparator_3_eq));  // open: gt, lt
  Comparator #(.width(32), .mode("unsigned")) comparator_4 (
    .a(ADDRESS), .b(32'h10012004), .eq(comparator_4_eq));  // open: gt, lt
  Comparator #(.width(32), .mode("unsigned")) comparator_5 (
    .a(ADDRESS), .b(32'h10013000), .eq(comparator_5_eq));  // open: gt, lt
  and and_1 (out_11, comparator_1_eq, MW);
  and and_2 (out_13, comparator_1_eq, MR);
  and and_3 (out_18, comparator_2_eq, MW);
  REG_Compatible2 reg_compatible2_1 (.out_4(reg_compatible2_1_out_4), .in_3(CLK), .in_2(1'b1), .in_1(Xcoord));
  assign bit_extender_1_out = {{1{comparator_3_eq}}, comparator_3_eq};  // Bit_Extender bit_extender_1
  REG_Compatible2 reg_compatible2_2 (.out_4(reg_compatible2_2_out_4), .in_3(CLK), .in_2(1'b1), .in_1(Ycoord));
  assign bit_extender_2_out = {{1{comparator_4_eq}}, comparator_4_eq};  // Bit_Extender bit_extender_2
  and and_4 (and_4_out, MW, comparator_5_eq);
  assign bit_extender_3_out = {{30{and_5_out[1]}}, and_5_out};  // Bit_Extender bit_extender_3
  assign and_5_out = reg_compatible2_1_out_4 & bit_extender_1_out;  // AND_Gate and_5, 2 bits wide
  assign bit_extender_4_out = {{30{and_6_out[1]}}, and_6_out};  // Bit_Extender bit_extender_4
  assign and_6_out = reg_compatible2_2_out_4 & bit_extender_2_out;  // AND_Gate and_6, 2 bits wide
  REG_Compatible8 reg_compatible8_1 (.out_4({HEXhigh, HEXlow}), .in_3(CLK), .in_2(and_4_out), .in_1(IN[7:0]));
  assign or_1_out = bit_extender_3_out | bit_extender_4_out;  // OR_Gate or_1, 32 bits wide
  or or_2 (or_2_out, comparator_3_eq, comparator_4_eq);
  Multiplexer #(.width(32), .enable("false")) multiplexer_1 (.in0(in_1), .in1(or_1_out), .out(OUT), .sel(or_2_out));

  assign out_9 = IN;
  assign out_10 = ADDRESS[13:2];
  assign out_12 = CLK;
  assign out_15 = IN;
  assign out_16 = ADDRESS[4:0];
  assign out_17 = CLK;
endmodule

module Add_Sub_afd4dc3a (
  input  sub,
  input  [31:0] A,
  input  [31:0] B,
  output [31:0] s,
  output ovf,
  output neg
);

  wire adder_1_cout, adder_2_cout;
  wire [31:0] bit_extender_1_out, xor_1_out;

  // Probe on bit_extender_1_out
  assign bit_extender_1_out = {{31{sub}}, sub};  // Bit_Extender bit_extender_1
  assign xor_1_out = bit_extender_1_out ^ B;  // XOR_Gate xor_1, 32 bits wide
  Adder #(.width(31)) adder_1 (.a(A[30:0]), .b(xor_1_out[30:0]), .out(s[30:0]), .cin(sub), .cout(adder_1_cout));
  Adder #(.width(1)) adder_2 (.a(A[31]), .b(xor_1_out[31]), .out(s[31]), .cin(adder_1_cout), .cout(adder_2_cout));
  xor xor_2 (ovf, adder_2_cout, adder_1_cout);
  ExactlyOne xor_3 (.out(neg), .in0(adder_2_cout), .in1(A[31]), .in2(xor_1_out[31]));
endmodule

module Logic (
  input  [31:0] A,
  input  [31:0] B,
  input  Ctrl_0_da297926,
  input  Ctrl_1_32ed63a7,
  output [31:0] s
);

  wire [31:0] and_1_out, multiplexer_1_out, multiplexer_3_out, or_1_out, xor_1_out;

  assign and_1_out = A & B;  // AND_Gate and_1, 32 bits wide
  assign or_1_out = A | B;  // OR_Gate or_1, 32 bits wide
  assign xor_1_out = A ^ B;  // XOR_Gate xor_1, 32 bits wide
  Multiplexer #(.width(32), .enable("false")) multiplexer_1 (
    .in0(and_1_out), .in1(or_1_out), .out(multiplexer_1_out), .sel(Ctrl_0_da297926));
  Multiplexer #(.width(32), .enable("false")) multiplexer_2 (
    .in0(multiplexer_1_out), .in1(multiplexer_3_out), .out(s), .sel(Ctrl_1_32ed63a7));
  Multiplexer #(.width(32), .enable("false")) multiplexer_3 (
    .in0(xor_1_out), .in1({B[15:0], {16{1'b0}}}), .out(multiplexer_3_out), .sel(Ctrl_0_da297926));
endmodule

module Comp (
  input  Cntr_0_f61f8da8,
  input  Cntr_1_d2d4e059,
  input  Cntr_2_8326bf86,
  input  [31:0] isum,
  input  neg,
  output [31:0] s
);

  wire and_1_out, and_2_out, and_3_out, comparator_1_eq, nor_1_out, or_1_out;

  Comparator #(.width(32), .mode("unsigned")) comparator_1 (
    .a({32{1'b0}}), .b(isum), .eq(comparator_1_eq));  // open: gt, lt
  nor nor_1 (nor_1_out, neg, comparator_1_eq);
  and and_1 (and_1_out, Cntr_0_f61f8da8, nor_1_out);
  and and_2 (and_2_out, Cntr_1_d2d4e059, comparator_1_eq);
  and and_3 (and_3_out, Cntr_2_8326bf86, neg);
  or or_1 (or_1_out, and_1_out, and_2_out);
  or or_2 (s[0], or_1_out, and_3_out);

  assign s[31:1] = {31{1'b0}};
endmodule

module ALU (
  input  [4:0] \type ,
  input  [31:0] X,
  input  [31:0] Y,
  output [31:0] Z
);

  wire add_sub_afd4dc3a_1_neg;
  wire [31:0] add_sub_afd4dc3a_1_s, comp_1_s, logic_1_s, multiplexer_1_out;

  Logic logic_1 (.A(X), .B(Y), .Ctrl_0_da297926(\type [2]), .Ctrl_1_32ed63a7(\type [3]), .s(logic_1_s));
  Comp comp_1 (
    .Cntr_0_f61f8da8(\type [2]), .Cntr_1_d2d4e059(\type [3]), .Cntr_2_8326bf86(\type [4]),
    .isum(add_sub_afd4dc3a_1_s), .neg(add_sub_afd4dc3a_1_neg), .s(comp_1_s));
  Add_Sub_afd4dc3a add_sub_afd4dc3a_1 (
    .sub(\type [1]), .A(X), .B(Y), .s(add_sub_afd4dc3a_1_s), .neg(add_sub_afd4dc3a_1_neg));  // open: ovf
  Multiplexer #(.width(32), .enable("false")) multiplexer_1 (
    .in0(logic_1_s), .in1(comp_1_s), .out(multiplexer_1_out), .sel(\type [1]));
  Multiplexer #(.width(32), .enable("false")) multiplexer_2 (
    .in0(multiplexer_1_out), .in1(add_sub_afd4dc3a_1_s), .out(Z), .sel(\type [0]));
endmodule

module Shifter (
  input  [31:0] X,
  input  right,
  input  shift,
  output [31:0] Z
);

  wire [31:0] multiplexer_2_out, shifter_1_out, shifter_2_out;

  Shifter_part #(.width(32)) shifter_1 (.in(X), .\dist (5'b00001), .out(shifter_1_out));
  Shifter_part #(.width(32), .shift("lr")) shifter_2 (.in(X), .\dist (5'b00001), .out(shifter_2_out));
  Multiplexer #(.width(32), .enable("false")) multiplexer_1 (.in0(X), .in1(multiplexer_2_out), .out(Z), .sel(shift));
  Multiplexer #(.width(32), .enable("false")) multiplexer_2 (
    .in0(shifter_1_out), .in1(shifter_2_out), .out(multiplexer_2_out), .sel(right));
endmodule

module SingleCycleDLX (
  input  Clk
);

  wire control_1_btaken, control_1_csel, control_1_dintsel, control_1_gpr_we, control_1_ji, control_1_jr,
       control_1_mr, control_1_mw, control_1_right, control_1_shift, control_1_sub, gprenv_1_aeq,
       gprenv_1_clkout, gprenv_1_gpr_we_out, irenv_1_jal, memenv_1_clko, memenv_1_ldo, memenv_1_stro,
       memenv_2_clko, memenv_2_ldo, memenv_2_stro;
  wire [1:0] control_1_type0;
  wire [2:0] control_1_type42;
  wire [4:0] gprenv_1_cadrout, irenv_1_aadr, irenv_1_badr, irenv_1_cadr;
  wire [5:0] irenv_1_function, irenv_1_opcode;
  wire [11:0] memenv_1_ma, memenv_2_ma;
  wire [31:0] adder_1_out, adder_2_out, alu_1_z, gprenv_1_a, gprenv_1_b, gprenv_1_cout, irenv_1_imm,
       memenv_1_out, memenv_2_mdi, memenv_2_out, multiplexer_1_out, multiplexer_2_out, multiplexer_3_out,
       multiplexer_4_out, multiplexer_5_out, multiplexer_6_out, multiplexer_7_out, ram_2_dout,
       reg_compatible_1_data_out, rom_1_data, shifter_1_out, shifter_2_z;

  REG_Compatible reg_compatible_1 (
    .Data_Out(reg_compatible_1_data_out), .WE(1'b1), .clk(Clk), .Data_In(multiplexer_4_out));
  Clock clock_1 ();  // open: out
  // Probe on reg_compatible_1_data_out
  Adder #(.width(32)) adder_1 (.a(32'h4), .b(reg_compatible_1_data_out), .out(adder_1_out));  // open: cin, cout
  MEMenv memenv_1 (
    .IN({32{1'b0}}), .ADDRESS(reg_compatible_1_data_out), .MW(1'b0), .MR(1'b1), .OUT(memenv_1_out),
    .CLK(Clk), .MA(memenv_1_ma), .MDO(rom_1_data), .clkO(memenv_1_clko), .strO(memenv_1_stro),
    .ldO(memenv_1_ldo));  // open: MDI
  // Probe on memenv_1_ma
  ROM #(.addrWidth(12), .dataWidth(32)) rom_1 (.addr(memenv_1_ma), .data(rom_1_data));
  // Probe on memenv_1_out
  // Probe on adder_1_out
  // Probe on rom_1_data
  // Probe on irenv_1_imm
  IRenv irenv_1 (
    .DI(memenv_1_out), .\function (irenv_1_function), .Cadr(irenv_1_cadr), .Badr(irenv_1_badr),
    .Aadr(irenv_1_aadr), .opcode(irenv_1_opcode), .Imm(irenv_1_imm), .JAL(irenv_1_jal));  // open: Inst
  // Probe on multiplexer_4_out
  Shifter_part #(.width(32)) shifter_1 (.in(irenv_1_imm), .\dist (5'b00010), .out(shifter_1_out));
  Multiplexer #(.width(32), .enable("false")) multiplexer_1 (
    .in0(multiplexer_7_out), .in1(adder_1_out), .out(multiplexer_1_out), .sel(irenv_1_jal));
  // Probe on gprenv_1_b
  // Probe on gprenv_1_a
  Control control_1 (
    .opcode(irenv_1_opcode), .func(irenv_1_function), .shift(control_1_shift), .ji(control_1_ji),
    .jr(control_1_jr), .MW(control_1_mw), .MR(control_1_mr), .csel(control_1_csel),
    .GPR_WE(control_1_gpr_we), .right(control_1_right), .DINTsel(control_1_dintsel), .sub(control_1_sub),
    .type42(control_1_type42), .type0(control_1_type0[0]), .AEQ(gprenv_1_aeq), .type1(control_1_type0[1]),
    .btaken(control_1_btaken));  // open: branch, Rtype, Itype, bnez, bsel
  Multiplexer #(.width(32), .enable("false")) multiplexer_2 (
    .in0(adder_1_out), .in1(32'h400000), .out(multiplexer_2_out), .sel(control_1_ji));
  // Probe on shifter_1_out
  GPRenv gprenv_1 (
    .C(multiplexer_1_out), .CLK(Clk), .GPR_WE(control_1_right), .Cadr(irenv_1_cadr), .Aadr(irenv_1_aadr),
    .Badr(irenv_1_badr), .A(gprenv_1_a), .B(gprenv_1_b), .AEQ(gprenv_1_aeq), .ClkOut(gprenv_1_clkout),
    .Cout(gprenv_1_cout), .GPR_WE_out(gprenv_1_gpr_we_out), .CadrOut(gprenv_1_cadrout));
  RAM #(.addrWidth(5), .dataWidth(32)) ram_1 (
    .addr(gprenv_1_cadrout), .we(gprenv_1_gpr_we_out), .oe(1'b0), .clk(gprenv_1_clkout), .data(gprenv_1_cout));
  Adder #(.width(32)) adder_2 (.a(multiplexer_2_out), .b(shifter_1_out), .out(adder_2_out));  // open: cin, cout
  Multiplexer #(.width(32), .enable("false")) multiplexer_3 (
    .in0(multiplexer_2_out), .in1(adder_2_out), .out(multiplexer_3_out), .sel(control_1_btaken));
  Multiplexer #(.width(32), .enable("false")) multiplexer_4 (
    .in0(multiplexer_3_out), .in1(gprenv_1_a), .out(multiplexer_4_out), .sel(control_1_jr));
  // Probe on gprenv_1_b
  // Probe on gprenv_1_a
  // Probe on multiplexer_5_out
  Multiplexer #(.width(32), .enable("false")) multiplexer_5 (
    .in0(gprenv_1_b), .in1(irenv_1_imm), .out(multiplexer_5_out), .sel(control_1_mw));
  // Probe on multiplexer_7_out
  ALU alu_1 (.\type ({control_1_type42, control_1_type0}), .X(gprenv_1_a), .Y(multiplexer_5_out), .Z(alu_1_z));
  Shifter shifter_2 (.X(gprenv_1_a), .right(control_1_dintsel), .shift(control_1_shift), .Z(shifter_2_z));
  // Probe on multiplexer_6_out
  Multiplexer #(.width(32), .enable("false")) multiplexer_6 (
    .in0(alu_1_z), .in1(shifter_2_z), .out(multiplexer_6_out), .sel(control_1_sub));
  Multiplexer #(.width(32), .enable("false")) multiplexer_7 (
    .in0(multiplexer_6_out), .in1(memenv_2_out), .out(multiplexer_7_out), .sel(control_1_gpr_we));
  MEMenv memenv_2 (
    .IN(gprenv_1_b), .ADDRESS(multiplexer_6_out), .MW(control_1_mr), .MR(control_1_csel), .OUT(memenv_2_out),
    .CLK(Clk), .MA(memenv_2_ma), .MDO(ram_2_dout), .clkO(memenv_2_clko), .MDI(memenv_2_mdi),
    .strO(memenv_2_stro), .ldO(memenv_2_ldo));
  RAM #(.addrWidth(12), .dataWidth(32), .trigger("falling"), .databus("bibus")) ram_2 (
    .addr(memenv_2_ma), .we(memenv_2_stro), .oe(memenv_2_ldo), .clk(memenv_2_clko), .din(memenv_2_mdi),
    .dout(ram_2_dout));

  // Notes on the sheet:
  //   PC
  //   contents of rom_1 (hex, n*v repeats v):
  //   3c011001 34290000 200b270f ad2b0004 8d2c0004 2149007f 2001007f 1414822 3149007f 3549007f 3949007f
  //   3c09007f 2949007f 11200001 0 15200001 0 112a0001 0 152a0001 0 8100017 0 c100018 0 3c010040 34290074
  //   1200008 0 3c010040 34290084 120f809 0 a4840 a4842 14b4820 14b4822 14b4824 14b4825 14b4826
  //   Instruction
  //   memory
  //   opcode
  //   IR
  //   env
  //   function
  //   GPR_WE
  //   ji
  //   Registers
  //   btaken
  //   jr
  //   Bsel
  //   right
  //   type[4:0]
  //   shift
  //   Csel
  //   DINTsel
  //   MW
  //   MR
  //   Data
  //   memory
endmodule

module Control (
  input  [5:0] opcode,
  input  [5:0] func,
  input  AEQ,
  output Itype,
  output Rtype,
  output branch,
  output shift,
  output ji,
  output bnez,
  output jr,
  output bsel,
  output MW,
  output MR,
  output csel,
  output GPR_WE,
  output right,
  output DINTsel,
  output sub,
  output [2:0] type42,
  output type1,
  output type0,
  output btaken
);

  wire and_1_out, and_2_out, and_3_out, and_4_out, and_6_out, and_7_out, and_8_out, and_9_out, and_10_out,
       and_11_out, and_12_out, and_15_out, and_16_out, and_18_out, comparator_3_eq, comparator_4_eq,
       comparator_5_eq, comparator_6_eq, comparator_7_eq, comparator_8_eq, comparator_9_eq, comparator_10_eq,
       comparator_11_eq, comparator_12_eq, comparator_13_eq, comparator_14_eq, comparator_15_eq,
       comparator_16_eq, comparator_17_eq, comparator_18_eq, comparator_19_eq, comparator_20_eq,
       comparator_21_eq, comparator_22_eq, nor_2_out, nor_3_out, not_1_out, not_2_out, not_3_out, not_4_out,
       not_5_out, not_6_out, not_7_out, not_8_out, not_9_out, not_10_out, not_11_out, not_12_out, not_14_out,
       not_15_out, or_1_out, or_3_out, or_12_out, xor_1_out;
  wire [2:0] multiplexer_1_out;

  Comparator #(.width(6), .mode("unsigned")) comparator_1 (.a(opcode), .b(6'b100011), .eq(csel));  // open: gt, lt
  Comparator #(.width(6), .mode("unsigned")) comparator_2 (.a(opcode), .b(6'b101011), .eq(MW));  // open: gt, lt
  Comparator #(.width(6), .mode("unsigned")) comparator_3 (
    .a(opcode), .b(6'b001000), .eq(comparator_3_eq));  // open: gt, lt
  Comparator #(.width(6), .mode("unsigned")) comparator_4 (
    .a(opcode), .b(6'b001100), .eq(comparator_4_eq));  // open: gt, lt
  Comparator #(.width(6), .mode("unsigned")) comparator_5 (
    .a(opcode), .b(6'b001101), .eq(comparator_5_eq));  // open: gt, lt
  Comparator #(.width(6), .mode("unsigned")) comparator_6 (
    .a(opcode), .b(6'b001110), .eq(comparator_6_eq));  // open: gt, lt
  Comparator #(.width(6), .mode("unsigned")) comparator_7 (
    .a(opcode), .b(6'b001111), .eq(comparator_7_eq));  // open: gt, lt
  Comparator #(.width(6), .mode("unsigned")) comparator_8 (
    .a(opcode), .b(6'b001010), .eq(comparator_8_eq));  // open: gt, lt
  Comparator #(.width(6), .mode("unsigned")) comparator_9 (
    .a(opcode), .b(6'b000100), .eq(comparator_9_eq));  // open: gt, lt
  Comparator #(.width(6), .mode("unsigned")) comparator_10 (
    .a(opcode), .b(6'b000101), .eq(comparator_10_eq));  // open: gt, lt
  Comparator #(.width(6), .mode("unsigned")) comparator_11 (
    .a(opcode), .b(6'b000010), .eq(comparator_11_eq));  // open: gt, lt
  Comparator #(.width(6), .mode("unsigned")) comparator_12 (
    .a(opcode), .b(6'b000011), .eq(comparator_12_eq));  // open: gt, lt
  Comparator #(.width(6), .mode("unsigned")) comparator_13 (
    .a(opcode), .b({6{1'b0}}), .eq(comparator_13_eq));  // open: gt, lt
  Comparator #(.width(6), .mode("unsigned")) comparator_14 (
    .a(func), .b(6'b001000), .eq(comparator_14_eq));  // open: gt, lt
  Comparator #(.width(6), .mode("unsigned")) comparator_15 (
    .a(func), .b(6'b001001), .eq(comparator_15_eq));  // open: gt, lt
  Comparator #(.width(6), .mode("unsigned")) comparator_16 (
    .a(func), .b({6{1'b0}}), .eq(comparator_16_eq));  // open: gt, lt
  Comparator #(.width(6), .mode("unsigned")) comparator_17 (
    .a(func), .b(6'b000010), .eq(comparator_17_eq));  // open: gt, lt
  Comparator #(.width(6), .mode("unsigned")) comparator_18 (
    .a(func), .b(6'b100000), .eq(comparator_18_eq));  // open: gt, lt
  Comparator #(.width(6), .mode("unsigned")) comparator_19 (
    .a(func), .b(6'b100010), .eq(comparator_19_eq));  // open: gt, lt
  Comparator #(.width(6), .mode("unsigned")) comparator_20 (
    .a(func), .b(6'b100100), .eq(comparator_20_eq));  // open: gt, lt
  Comparator #(.width(6), .mode("unsigned")) comparator_21 (
    .a(func), .b(6'b110101), .eq(comparator_21_eq));  // open: gt, lt
  Comparator #(.width(6), .mode("unsigned")) comparator_22 (
    .a(func), .b(6'b110110), .eq(comparator_22_eq));  // open: gt, lt
  and and_1 (and_1_out, comparator_13_eq, comparator_14_eq, comparator_15_eq, comparator_16_eq, comparator_17_eq, comparator_18_eq, comparator_19_eq, comparator_20_eq, comparator_21_eq, comparator_22_eq);
  or or_1 (or_1_out, csel, MW, comparator_3_eq, comparator_4_eq, comparator_5_eq, comparator_6_eq, comparator_7_eq, comparator_8_eq, comparator_9_eq, comparator_10_eq, comparator_13_eq);
  not not_1 (not_1_out, or_1_out);
  not not_2 (not_2_out, MW);
  not not_3 (not_3_out, comparator_9_eq);
  not not_4 (not_4_out, comparator_10_eq);
  not not_5 (not_5_out, comparator_11_eq);
  and and_2 (and_2_out, comparator_13_eq, comparator_14_eq);
  not not_6 (not_6_out, and_2_out);
  not not_7 (not_7_out, comparator_13_eq);
  and and_3 (and_3_out, comparator_13_eq, comparator_15_eq);
  and and_4 (and_4_out, comparator_13_eq, comparator_16_eq);
  and and_5 (right, comparator_13_eq, comparator_17_eq);
  and and_6 (and_6_out, comparator_13_eq, comparator_18_eq);
  and and_7 (and_7_out, comparator_13_eq, comparator_19_eq);
  and and_8 (and_8_out, comparator_13_eq, comparator_20_eq);
  and and_9 (and_9_out, comparator_13_eq, comparator_21_eq);
  and and_10 (and_10_out, comparator_13_eq, comparator_22_eq);
  not not_8 (not_8_out, comparator_9_eq);
  not not_9 (not_9_out, comparator_11_eq);
  not not_10 (not_10_out, comparator_12_eq);
  not not_11 (not_11_out, comparator_13_eq);
  not not_12 (not_12_out, comparator_10_eq);
  nor nor_1 (Rtype, opcode[0], opcode[1], opcode[2], opcode[3], opcode[4], opcode[5]);
  nor nor_2 (nor_2_out, opcode[4], opcode[3], opcode[5]);
  nor nor_3 (nor_3_out, func[2], func[3], func[4], func[5]);
  or or_2 (ji, not_1_out, comparator_11_eq, comparator_12_eq, and_1_out);
  and and_11 (and_11_out, not_8_out, not_9_out, not_10_out, not_11_out);
  and and_12 (and_12_out, not_2_out, not_3_out, not_4_out, not_5_out, not_7_out, not_12_out, not_6_out);
  or or_3 (or_3_out, csel, comparator_3_eq, comparator_4_eq, comparator_5_eq, comparator_6_eq, comparator_7_eq, comparator_8_eq, and_3_out, and_4_out, right, and_6_out, and_7_out, and_8_out, and_9_out, and_10_out);
  not not_13 (Itype, Rtype);
  and and_13 (branch, Itype, nor_2_out);
  and and_14 (shift, Rtype, nor_3_out);
  or or_4 (bnez, and_11_out, comparator_10_eq);
  and and_15 (and_15_out, comparator_13_eq, comparator_14_eq);
  and and_16 (and_16_out, comparator_13_eq, comparator_15_eq);
  or or_5 (bsel, MW, comparator_10_eq, comparator_3_eq, comparator_4_eq, comparator_5_eq, comparator_6_eq, comparator_7_eq, comparator_8_eq);
  Multiplexer #(.select(3), .width(3), .enable("false")) multiplexer_1 (
    .in0(func[2:0]), .in2(3'b100), .in4(opcode[2:0]), .in5(opcode[2:0]), .in6(opcode[2:0]),
    .in7(opcode[2:0]), .out(multiplexer_1_out), .sel(opcode[2:0]));  // open: in1, in3
  assign type42 = multiplexer_1_out;  // OR_Gate or_6, 3 bits wide OR_Gate
  or or_7 (type0, comparator_3_eq, MW, csel, and_6_out, and_7_out);
  or or_8 (jr, and_15_out, and_16_out);
  or or_9 (GPR_WE, and_12_out, or_3_out);
  or or_10 (DINTsel, and_4_out, right);
  or or_11 (sub, and_7_out, comparator_8_eq);
  xor xor_1 (xor_1_out, AEQ, bnez);
  or or_12 (or_12_out, ji, xor_1_out);
  not not_14 (not_14_out, opcode[4]);
  not not_15 (not_15_out, opcode[5]);
  and and_17 (btaken, branch, or_12_out);
  and and_18 (and_18_out, not_14_out, opcode[3], not_15_out);
  or or_13 (type1, and_18_out, sub);

  assign MR = csel;
endmodule

module L_32bitwiseAND_63a49550 (
  input  in_1,
  input  in_2,
  input  in_3,
  input  in_4,
  input  in_5,
  input  in_6,
  input  in_7,
  input  in_8,
  input  in_9,
  input  in_10,
  input  in_11,
  input  in_12,
  input  in_13,
  input  in_14,
  input  in_15,
  input  in_16,
  input  enable,
  input  in_18,
  input  in_19,
  input  in_20,
  input  in_21,
  input  in_22,
  input  in_23,
  input  in_24,
  input  in_25,
  input  in_26,
  input  in_27,
  input  in_28,
  input  in_29,
  input  in_30,
  input  in_31,
  input  in_32,
  input  in_33,
  output out_34,
  output out_35,
  output out_36,
  output out_37,
  output out_38,
  output out_39,
  output out_40,
  output out_41,
  output out_42,
  output out_43,
  output out_44,
  output out_45,
  output out_46,
  output out_47,
  output out_48,
  output out_49,
  output out_50,
  output out_51,
  output out_52,
  output out_53,
  output out_54,
  output out_55,
  output out_56,
  output out_57,
  output out_58,
  output out_59,
  output out_60,
  output out_61,
  output out_62,
  output out_63,
  output out_64,
  output out_65
);

  wire [31:0] bit_extender_1_out;

  assign bit_extender_1_out = {{31{enable}}, enable};  // Bit_Extender bit_extender_1
  assign {out_50, out_34, out_51, out_35, out_52, out_36, out_53, out_37, out_54, out_38, out_55, out_39, out_56, out_40, out_57, out_41, out_58, out_42, out_59, out_43, out_60, out_44, out_61, out_45, out_62, out_46, out_63, out_47, out_64, out_48, out_65, out_49} = bit_extender_1_out & {in_1, in_18, in_2, in_19, in_3, in_20, in_4, in_21, in_5, in_22, in_6, in_23, in_7, in_24, in_8, in_25, in_9, in_26, in_10, in_27, in_11, in_28, in_12, in_29, in_13, in_30, in_14, in_31, in_15, in_32, in_16, in_33};  // AND_Gate and_1, 32 bits wide
endmodule

module ParallelReadOutReg (
  input  [31:0] in_1,
  input  in_2,
  input  Enable,
  input  [4:0] in_4,
  output [31:0] out_5,
  output [31:0] out_6,
  output [31:0] out_7,
  output [31:0] out_8,
  output [31:0] out_9,
  output [31:0] out_10,
  output [31:0] out_11,
  output [31:0] out_12,
  output [31:0] out_13,
  output [31:0] out_14,
  output [31:0] out_15,
  output [31:0] out_16,
  output [31:0] out_17,
  output [31:0] out_18,
  output [31:0] out_19,
  output [31:0] out_20,
  output [31:0] out_21,
  output [31:0] out_22,
  output [31:0] out_23,
  output [31:0] out_24,
  output [31:0] out_25,
  output [31:0] out_26,
  output [31:0] out_27,
  output [31:0] out_28,
  output [31:0] out_29,
  output [31:0] out_30,
  output [31:0] out_31,
  output [31:0] out_32,
  output [31:0] out_33,
  output [31:0] out_34,
  output [31:0] out_35,
  output [31:0] out_36,
  output [31:0] out_37
);

  wire decoder_1_out0, decoder_1_out1, decoder_1_out2, decoder_1_out3, decoder_1_out4, decoder_1_out5,
       decoder_1_out6, decoder_1_out7, decoder_1_out8, decoder_1_out9, decoder_1_out10, decoder_1_out11,
       decoder_1_out12, decoder_1_out13, decoder_1_out14, decoder_1_out15, decoder_1_out16, decoder_1_out17,
       decoder_1_out18, decoder_1_out19, decoder_1_out20, decoder_1_out21, decoder_1_out22, decoder_1_out23,
       decoder_1_out24, decoder_1_out25, decoder_1_out26, decoder_1_out27, decoder_1_out28, decoder_1_out29,
       decoder_1_out30, decoder_1_out31, l_32bitwiseand_63a49550_1_out_34, l_32bitwiseand_63a49550_1_out_35,
       l_32bitwiseand_63a49550_1_out_37, l_32bitwiseand_63a49550_1_out_39, l_32bitwiseand_63a49550_1_out_41,
       l_32bitwiseand_63a49550_1_out_43, l_32bitwiseand_63a49550_1_out_45, l_32bitwiseand_63a49550_1_out_47,
       l_32bitwiseand_63a49550_1_out_49, l_32bitwiseand_63a49550_1_out_50, l_32bitwiseand_63a49550_1_out_51;

  Multiplexer #(.select(5), .width(32)) multiplexer_1 (
    .in0(out_5), .in1(out_13), .in2(out_21), .in3(out_29), .in4(out_6), .in5(out_14), .in6(out_22),
    .in7(out_30), .in8(out_7), .in9(out_15), .in10(out_23), .in11(out_31), .in12(out_8), .in13(out_16),
    .in14(out_24), .in15(out_32), .in16(out_9), .in17(out_17), .in18(out_25), .in19(out_33), .in20(out_10),
    .in21(out_18), .in22(out_26), .in23(out_34), .in24(out_11), .in25(out_19), .in26(out_27), .in27(out_35),
    .in28(out_12), .in29(out_20), .in30(out_28), .in31(out_36), .out(out_37), .sel(in_4));  // open: en
  REG_Compatible reg_compatible_1 (.Data_Out(out_5), .WE(l_32bitwiseand_63a49550_1_out_50), .clk(in_2), .Data_In(in_1));
  REG_Compatible reg_compatible_2 (
    .Data_Out(out_13), .WE(l_32bitwiseand_63a49550_1_out_34), .clk(in_2), .Data_In(in_1));
  REG_Compatible reg_compatible_3 (
    .Data_Out(out_21), .WE(l_32bitwiseand_63a49550_1_out_51), .clk(in_2), .Data_In(in_1));
  REG_Compatible reg_compatible_4 (
    .Data_Out(out_29), .WE(l_32bitwiseand_63a49550_1_out_35), .clk(in_2), .Data_In(in_1));
  REG_Compatible reg_compatible_5 (.Data_Out(out_6), .WE(in_2), .clk(in_2), .Data_In(in_1));
  REG_Compatible reg_compatible_6 (.Data_Out(out_14), .WE(in_2), .clk(in_2), .Data_In(in_1));
  REG_Compatible reg_compatible_7 (.Data_Out(out_22), .WE(in_2), .clk(in_2), .Data_In(in_1));
  REG_Compatible reg_compatible_8 (
    .Data_Out(out_30), .WE(l_32bitwiseand_63a49550_1_out_37), .clk(in_2), .Data_In(in_1));
  Decoder #(.select(5)) decoder_1 (
    .out0(decoder_1_out0), .out1(decoder_1_out1), .out2(decoder_1_out2), .out3(decoder_1_out3),
    .out4(decoder_1_out4), .out5(decoder_1_out5), .out6(decoder_1_out6), .out7(decoder_1_out7),
    .out8(decoder_1_out8), .out9(decoder_1_out9), .out10(decoder_1_out10), .out11(decoder_1_out11),
    .out12(decoder_1_out12), .out13(decoder_1_out13), .out14(decoder_1_out14), .out15(decoder_1_out15),
    .out16(decoder_1_out16), .out17(decoder_1_out17), .out18(decoder_1_out18), .out19(decoder_1_out19),
    .out20(decoder_1_out20), .out21(decoder_1_out21), .out22(decoder_1_out22), .out23(decoder_1_out23),
    .out24(decoder_1_out24), .out25(decoder_1_out25), .out26(decoder_1_out26), .out27(decoder_1_out27),
    .out28(decoder_1_out28), .out29(decoder_1_out29), .out30(decoder_1_out30), .out31(decoder_1_out31),
    .sel(in_4));  // open: en
  REG_Compatible reg_compatible_9 (.Data_Out(out_7), .WE(in_2), .clk(in_2), .Data_In(in_1));
  REG_Compatible reg_compatible_10 (.Data_Out(out_15), .WE(in_2), .clk(in_2), .Data_In(in_1));
  REG_Compatible reg_compatible_11 (.Data_Out(out_23), .WE(in_2), .clk(in_2), .Data_In(in_1));
  REG_Compatible reg_compatible_12 (
    .Data_Out(out_31), .WE(l_32bitwiseand_63a49550_1_out_39), .clk(in_2), .Data_In(in_1));
  REG_Compatible reg_compatible_13 (.Data_Out(out_8), .WE(in_2), .clk(in_2), .Data_In(in_1));
  REG_Compatible reg_compatible_14 (.Data_Out(out_16), .WE(in_2), .clk(in_2), .Data_In(in_1));
  REG_Compatible reg_compatible_15 (.Data_Out(out_24), .WE(in_2), .clk(in_2), .Data_In(in_1));
  REG_Compatible reg_compatible_16 (
    .Data_Out(out_32), .WE(l_32bitwiseand_63a49550_1_out_41), .clk(in_2), .Data_In(in_1));
  REG_Compatible reg_compatible_17 (.Data_Out(out_9), .WE(in_2), .clk(in_2), .Data_In(in_1));
  REG_Compatible reg_compatible_18 (.Data_Out(out_17), .WE(in_2), .clk(in_2), .Data_In(in_1));
  REG_Compatible reg_compatible_19 (.Data_Out(out_25), .WE(in_2), .clk(in_2), .Data_In(in_1));
  REG_Compatible reg_compatible_20 (
    .Data_Out(out_33), .WE(l_32bitwiseand_63a49550_1_out_43), .clk(in_2), .Data_In(in_1));
  L_32bitwiseAND_63a49550 l_32bitwiseand_63a49550_1 (
    .out_50(l_32bitwiseand_63a49550_1_out_50), .out_34(l_32bitwiseand_63a49550_1_out_34),
    .out_51(l_32bitwiseand_63a49550_1_out_51), .out_35(l_32bitwiseand_63a49550_1_out_35), .out_52(in_2),
    .out_36(in_2), .out_53(in_2), .out_37(l_32bitwiseand_63a49550_1_out_37), .out_54(in_2), .out_38(in_2),
    .out_55(in_2), .out_39(l_32bitwiseand_63a49550_1_out_39), .out_56(in_2), .out_40(in_2), .out_57(in_2),
    .out_41(l_32bitwiseand_63a49550_1_out_41), .out_58(in_2), .out_42(in_2), .out_59(in_2),
    .out_43(l_32bitwiseand_63a49550_1_out_43), .out_60(in_2), .out_44(in_2), .out_61(in_2),
    .out_45(l_32bitwiseand_63a49550_1_out_45), .out_62(in_2), .out_46(in_2), .out_63(in_2),
    .out_47(l_32bitwiseand_63a49550_1_out_47), .out_64(in_2), .out_48(in_2), .out_65(in_2),
    .out_49(l_32bitwiseand_63a49550_1_out_49), .enable(Enable), .in_1(decoder_1_out0),
    .in_18(decoder_1_out1), .in_2(decoder_1_out2), .in_19(decoder_1_out3), .in_3(decoder_1_out4),
    .in_20(decoder_1_out5), .in_4(decoder_1_out6), .in_21(decoder_1_out7), .in_5(decoder_1_out8),
    .in_22(decoder_1_out9), .in_6(decoder_1_out10), .in_23(decoder_1_out11), .in_7(decoder_1_out12),
    .in_24(decoder_1_out13), .in_8(decoder_1_out14), .in_25(decoder_1_out15), .in_9(decoder_1_out16),
    .in_26(decoder_1_out17), .in_10(decoder_1_out18), .in_27(decoder_1_out19), .in_11(decoder_1_out20),
    .in_28(decoder_1_out21), .in_12(decoder_1_out22), .in_29(decoder_1_out23), .in_13(decoder_1_out24),
    .in_30(decoder_1_out25), .in_14(decoder_1_out26), .in_31(decoder_1_out27), .in_15(decoder_1_out28),
    .in_32(decoder_1_out29), .in_16(decoder_1_out30), .in_33(decoder_1_out31));
  REG_Compatible reg_compatible_21 (.Data_Out(out_10), .WE(in_2), .clk(in_2), .Data_In(in_1));
  REG_Compatible reg_compatible_22 (.Data_Out(out_18), .WE(in_2), .clk(in_2), .Data_In(in_1));
  REG_Compatible reg_compatible_23 (.Data_Out(out_26), .WE(in_2), .clk(in_2), .Data_In(in_1));
  REG_Compatible reg_compatible_24 (
    .Data_Out(out_34), .WE(l_32bitwiseand_63a49550_1_out_45), .clk(in_2), .Data_In(in_1));
  REG_Compatible reg_compatible_25 (.Data_Out(out_11), .WE(in_2), .clk(in_2), .Data_In(in_1));
  REG_Compatible reg_compatible_26 (.Data_Out(out_19), .WE(in_2), .clk(in_2), .Data_In(in_1));
  REG_Compatible reg_compatible_27 (.Data_Out(out_27), .WE(in_2), .clk(in_2), .Data_In(in_1));
  REG_Compatible reg_compatible_28 (
    .Data_Out(out_35), .WE(l_32bitwiseand_63a49550_1_out_47), .clk(in_2), .Data_In(in_1));
  REG_Compatible reg_compatible_29 (.Data_Out(out_12), .WE(in_2), .clk(in_2), .Data_In(in_1));
  REG_Compatible reg_compatible_30 (.Data_Out(out_20), .WE(in_2), .clk(in_2), .Data_In(in_1));
  REG_Compatible reg_compatible_31 (.Data_Out(out_28), .WE(in_2), .clk(in_2), .Data_In(in_1));
  REG_Compatible reg_compatible_32 (
    .Data_Out(out_36), .WE(l_32bitwiseand_63a49550_1_out_49), .clk(in_2), .Data_In(in_1));
endmodule

module MEM2use (
  input  CLK,
  input  [31:0] IN,
  input  [31:0] ADDRESS,
  input  MW,
  input  MR,
  output [31:0] OUT
);

  wire clock_1_out, memenv2_1_out_11, memenv2_1_out_12, memenv2_1_out_13, memenv2_1_out_17, memenv2_1_out_18;
  wire [1:0] joystick_1_x, joystick_1_y;
  wire [3:0] memenv2_1_hexhigh, memenv2_1_hexlow;
  wire [4:0] memenv2_1_out_16;
  wire [11:0] memenv2_1_out_10;
  wire [31:0] memenv2_1_out_9, memenv2_1_out_15, parallelreadoutreg_1_out_5, parallelreadoutreg_1_out_6,
       parallelreadoutreg_1_out_7, parallelreadoutreg_1_out_8, parallelreadoutreg_1_out_9,
       parallelreadoutreg_1_out_10, parallelreadoutreg_1_out_11, parallelreadoutreg_1_out_12,
       parallelreadoutreg_1_out_13, parallelreadoutreg_1_out_14, parallelreadoutreg_1_out_15,
       parallelreadoutreg_1_out_16, parallelreadoutreg_1_out_17, parallelreadoutreg_1_out_18,
       parallelreadoutreg_1_out_19, parallelreadoutreg_1_out_20, parallelreadoutreg_1_out_21,
       parallelreadoutreg_1_out_22, parallelreadoutreg_1_out_23, parallelreadoutreg_1_out_24,
       parallelreadoutreg_1_out_25, parallelreadoutreg_1_out_26, parallelreadoutreg_1_out_27,
       parallelreadoutreg_1_out_28, parallelreadoutreg_1_out_29, parallelreadoutreg_1_out_30,
       parallelreadoutreg_1_out_31, parallelreadoutreg_1_out_32, parallelreadoutreg_1_out_33,
       parallelreadoutreg_1_out_34, parallelreadoutreg_1_out_35, parallelreadoutreg_1_out_36, ram_1_dout;

  Clock clock_1 (.out(clock_1_out));
  RAM #(.addrWidth(12), .dataWidth(32), .trigger("falling"), .databus("bibus")) ram_1 (
    .addr(memenv2_1_out_10), .we(memenv2_1_out_11), .oe(memenv2_1_out_13), .clk(memenv2_1_out_12),
    .din(memenv2_1_out_9), .dout(ram_1_dout));
  Hex_Digit_Display hex_digit_display_1 (.value(memenv2_1_hexhigh));  // open: dp
  MEMenv2 memenv2_1 (
    .IN(IN), .ADDRESS(ADDRESS), .MW(MW), .MR(MR), .CLK(clock_1_out), .OUT(OUT), .out_15(memenv2_1_out_15),
    .out_16(memenv2_1_out_16), .out_17(memenv2_1_out_17), .out_18(memenv2_1_out_18), .Ycoord(joystick_1_y),
    .HEXlow(memenv2_1_hexlow), .HEXhigh(memenv2_1_hexhigh), .out_10(memenv2_1_out_10),
    .out_9(memenv2_1_out_9), .out_11(memenv2_1_out_11), .out_12(memenv2_1_out_12), .out_13(memenv2_1_out_13),
    .in_1(ram_1_dout), .Xcoord(joystick_1_x));
  Hex_Digit_Display hex_digit_display_2 (.value(memenv2_1_hexlow));  // open: dp
  // Probe on joystick_1_y
  // Probe on joystick_1_x
  Joystick #(.bits(2)) joystick_1 (.x(joystick_1_x), .y(joystick_1_y));
  DotMatrix #(.inputtype("row"), .matrixcols(32), .matrixrows(32)) dotmatrix_1 (
    .row0(parallelreadoutreg_1_out_5), .row1(parallelreadoutreg_1_out_13),
    .row2(parallelreadoutreg_1_out_21), .row3(parallelreadoutreg_1_out_29),
    .row4(parallelreadoutreg_1_out_6), .row5(parallelreadoutreg_1_out_14),
    .row6(parallelreadoutreg_1_out_22), .row7(parallelreadoutreg_1_out_30),
    .row8(parallelreadoutreg_1_out_7), .row9(parallelreadoutreg_1_out_15),
    .row10(parallelreadoutreg_1_out_23), .row11(parallelreadoutreg_1_out_31),
    .row12(parallelreadoutreg_1_out_8), .row13(parallelreadoutreg_1_out_16),
    .row14(parallelreadoutreg_1_out_24), .row15(parallelreadoutreg_1_out_32),
    .row16(parallelreadoutreg_1_out_9), .row17(parallelreadoutreg_1_out_17),
    .row18(parallelreadoutreg_1_out_25), .row19(parallelreadoutreg_1_out_33),
    .row20(parallelreadoutreg_1_out_10), .row21(parallelreadoutreg_1_out_18),
    .row22(parallelreadoutreg_1_out_26), .row23(parallelreadoutreg_1_out_34),
    .row24(parallelreadoutreg_1_out_11), .row25(parallelreadoutreg_1_out_19),
    .row26(parallelreadoutreg_1_out_27), .row27(parallelreadoutreg_1_out_35),
    .row28(parallelreadoutreg_1_out_12), .row29(parallelreadoutreg_1_out_20),
    .row30(parallelreadoutreg_1_out_28), .row31(parallelreadoutreg_1_out_36));
  ParallelReadOutReg parallelreadoutreg_1 (
    .in_1(memenv2_1_out_15), .in_2(memenv2_1_out_17), .Enable(memenv2_1_out_18), .in_4(memenv2_1_out_16),
    .out_5(parallelreadoutreg_1_out_5), .out_6(parallelreadoutreg_1_out_6),
    .out_7(parallelreadoutreg_1_out_7), .out_8(parallelreadoutreg_1_out_8),
    .out_9(parallelreadoutreg_1_out_9), .out_10(parallelreadoutreg_1_out_10),
    .out_11(parallelreadoutreg_1_out_11), .out_12(parallelreadoutreg_1_out_12),
    .out_13(parallelreadoutreg_1_out_13), .out_14(parallelreadoutreg_1_out_14),
    .out_15(parallelreadoutreg_1_out_15), .out_16(parallelreadoutreg_1_out_16),
    .out_17(parallelreadoutreg_1_out_17), .out_18(parallelreadoutreg_1_out_18),
    .out_19(parallelreadoutreg_1_out_19), .out_20(parallelreadoutreg_1_out_20),
    .out_21(parallelreadoutreg_1_out_21), .out_29(parallelreadoutreg_1_out_29),
    .out_22(parallelreadoutreg_1_out_22), .out_30(parallelreadoutreg_1_out_30),
    .out_23(parallelreadoutreg_1_out_23), .out_31(parallelreadoutreg_1_out_31),
    .out_24(parallelreadoutreg_1_out_24), .out_32(parallelreadoutreg_1_out_32),
    .out_25(parallelreadoutreg_1_out_25), .out_33(parallelreadoutreg_1_out_33),
    .out_26(parallelreadoutreg_1_out_26), .out_34(parallelreadoutreg_1_out_34),
    .out_27(parallelreadoutreg_1_out_27), .out_35(parallelreadoutreg_1_out_35),
    .out_28(parallelreadoutreg_1_out_28), .out_36(parallelreadoutreg_1_out_36));  // open: out_37

  // Notes on the sheet:
  //   Data
  //   memory
endmodule
